// Logisim project CONTROL_UNITS.circ as structural Verilog
module PC (
  input  C,
  input  Z,
  input  T0,
  input  T1,
  input  T3,
  input  T4,
  input  M196,
  input  M197,
  input  M198,
  input  M199,
  input  M200,
  input  M201,
  input  M202,
  input  M203,
  input  M204,
  input  M205,
  input  M206,
  input  M207,
  input  M208,
  input  M209,
  input  M210,
  input  M211,
  input  M212,
  input  M213,
  output PC_BUS,
  output PC_INC,
  output PC_LOAD
);

  wire and_1_out, and_2_out, and_3_out, and_4_out, and_5_out, and_6_out, and_7_out, and_8_out, and_9_out,
       and_10_out, and_11_out, and_12_out, and_13_out, and_14_out, and_15_out, and_16_out, and_17_out,
       or_1_out, or_2_out;

  and and_1 (and_1_out, M199, Z);
  and and_2 (and_2_out, M202, ~Z);  // AND_Gate
  and and_3 (and_3_out, M205, C, ~Z);  // AND_Gate
  and and_4 (and_4_out, M208, ~C, Z);  // AND_Gate
  and and_5 (and_5_out, M211, Z, C);
  and and_6 (and_6_out, M200, Z);
  and and_7 (and_7_out, M201, Z);
  and and_8 (and_8_out, M203, ~Z);  // AND_Gate
  and and_9 (and_9_out, M204, ~Z);  // AND_Gate
  and and_10 (and_10_out, M206, C, ~Z);  // AND_Gate
  and and_11 (and_11_out, M207, C, ~Z);  // AND_Gate
  and and_12 (and_12_out, M209, ~C, Z);  // AND_Gate
  and and_13 (and_13_out, M210, ~C, Z);  // AND_Gate
  and and_14 (and_14_out, M212, C, Z);
  and and_15 (and_15_out, M213, C, Z);
  or or_1 (or_1_out, M196, and_1_out, and_2_out, and_3_out, and_4_out, and_5_out);
  and and_16 (and_16_out, or_1_out, T4);
  or or_2 (or_2_out, M197, M198, and_6_out, and_7_out, and_8_out, and_9_out, and_10_out, and_11_out, and_12_out, and_13_out, and_14_out, and_15_out);
  and and_17 (and_17_out, or_2_out, T3);
  or or_3 (PC_LOAD, and_16_out, and_17_out);

  assign PC_BUS = T0;
  assign PC_INC = T1;
endmodule

module IR (
  input  T1,
  input  T2,
  input  T3,
  input  M190,
  input  M191,
  input  M192,
  input  M193,
  input  M194,
  output IR_BUS,
  output IR_LOAD
);

  wire and_1_out, or_1_out;

  or or_1 (or_1_out, M194, M193, M192, M191, M190);
  and and_1 (and_1_out, or_1_out, T3);
  or or_2 (IR_BUS, and_1_out, T2);

  assign IR_LOAD = T1;
endmodule

module AR (
  input  C,
  input  Z,
  input  T0,
  input  T2,
  input  T3,
  input  T4,
  input  M0,
  input  M1,
  input  M2,
  input  M3,
  input  M4,
  input  M17,
  input  M18,
  input  M19,
  input  M20,
  input  M21,
  input  M34,
  input  M35,
  input  M36,
  input  M37,
  input  M38,
  input  M51,
  input  M52,
  input  M53,
  input  M54,
  input  M55,
  input  M68,
  input  M69,
  input  M70,
  input  M71,
  input  M72,
  input  M85,
  input  M86,
  input  M87,
  input  M88,
  input  M89,
  input  M102,
  input  M103,
  input  M104,
  input  M105,
  input  M106,
  input  M119,
  input  M120,
  input  M121,
  input  M122,
  input  M123,
  input  M136,
  input  M137,
  input  M138,
  input  M139,
  input  M140,
  input  M153,
  input  M154,
  input  M155,
  input  M156,
  input  M157,
  input  M170,
  input  M171,
  input  M172,
  input  M173,
  input  M174,
  input  M180,
  input  M181,
  input  M182,
  input  M183,
  input  M184,
  input  M196,
  input  M197,
  input  M199,
  input  M200,
  input  M202,
  input  M203,
  input  M205,
  input  M206,
  input  M208,
  input  M209,
  input  M211,
  input  M212,
  output AR_LOAD,
  output AR_BUS
);

  wire and_1_out, and_2_out, and_3_out, and_4_out, and_5_out, and_6_out, and_7_out, and_8_out, and_9_out,
       and_10_out, and_11_out, and_12_out, and_13_out, or_1_out, or_2_out, or_3_out, or_4_out;

  and and_1 (and_1_out, M196, T4);
  and and_2 (and_2_out, M197, T3);
  and and_3 (and_3_out, M199, T4, Z);
  and and_4 (and_4_out, M200, T3, Z);
  and and_5 (and_5_out, M202, T4, ~Z);  // AND_Gate
  and and_6 (and_6_out, M203, T3, ~Z);  // AND_Gate
  and and_7 (and_7_out, M205, T4, ~Z, C);  // AND_Gate
  and and_8 (and_8_out, M206, T3, ~Z, C);  // AND_Gate
  and and_9 (and_9_out, M208, T4, Z, ~C);  // AND_Gate
  and and_10 (and_10_out, M209, T3, Z, ~C);  // AND_Gate
  and and_11 (and_11_out, M211, T4, Z, C);
  and and_12 (and_12_out, M212, T3, Z, C);
  or or_1 (or_1_out, M211, M208, M205, M202, M199, M196, M184, M183, M182, M181, M180, M174, M173, M172, M171, M170, M157, M156, M155, M154, M153, M140);
  or or_2 (or_2_out, M139, M138, M137, M136, M123, M122, M121, M120, M119, M106, M105, M104, M103, M102, M89, M88, M87, M86, M85, M72, M71, M70);
  or or_3 (or_3_out, M69, M68, M55, M54, M53, M52, M51, M38, M37, M36, M35, M34, M21, M20, M19, M18, M17, M4, M3, M2, M1, M0);
  or or_4 (or_4_out, or_1_out, or_2_out, or_3_out);
  or or_5 (AR_BUS, and_1_out, and_2_out, and_3_out, and_4_out, and_5_out, and_6_out, and_7_out, and_8_out, and_9_out, and_10_out, and_11_out, and_12_out);
  and and_13 (and_13_out, or_4_out, T3);
  or or_6 (AR_LOAD, and_13_out, T2, T0);
endmodule

module DR (
  input  T3,
  input  T4,
  input  T5,
  input  M0,
  input  M1,
  input  M2,
  input  M3,
  input  M4,
  input  M5,
  input  M6,
  input  M7,
  input  M8,
  input  M9,
  input  M15,
  input  M17,
  input  M18,
  input  M19,
  input  M20,
  input  M21,
  input  M22,
  input  M23,
  input  M24,
  input  M25,
  input  M26,
  input  M32,
  input  M34,
  input  M35,
  input  M36,
  input  M37,
  input  M38,
  input  M39,
  input  M40,
  input  M41,
  input  M42,
  input  M43,
  input  M49,
  input  M51,
  input  M52,
  input  M53,
  input  M54,
  input  M55,
  input  M56,
  input  M57,
  input  M58,
  input  M59,
  input  M60,
  input  M66,
  input  M68,
  input  M69,
  input  M70,
  input  M71,
  input  M72,
  input  M73,
  input  M74,
  input  M75,
  input  M76,
  input  M77,
  input  M83,
  input  M85,
  input  M86,
  input  M87,
  input  M88,
  input  M89,
  input  M90,
  input  M91,
  input  M92,
  input  M93,
  input  M94,
  input  M100,
  input  M102,
  input  M103,
  input  M104,
  input  M105,
  input  M106,
  input  M107,
  input  M108,
  input  M109,
  input  M110,
  input  M111,
  input  M117,
  input  M119,
  input  M120,
  input  M121,
  input  M122,
  input  M123,
  input  M124,
  input  M125,
  input  M126,
  input  M127,
  input  M128,
  input  M134,
  input  M136,
  input  M137,
  input  M138,
  input  M139,
  input  M140,
  input  M141,
  input  M142,
  input  M143,
  input  M144,
  input  M145,
  input  M151,
  input  M153,
  input  M154,
  input  M155,
  input  M156,
  input  M157,
  input  M158,
  input  M159,
  input  M160,
  input  M161,
  input  M162,
  input  M168,
  input  M170,
  input  M171,
  input  M172,
  input  M173,
  input  M174,
  input  M175,
  input  M176,
  input  M177,
  input  M178,
  input  M179,
  output DR_LOAD,
  output DR_BUS
);

  wire and_1_out, and_2_out, and_3_out, and_4_out, or_1_out, or_2_out, or_3_out, or_4_out, or_5_out,
       or_6_out, or_7_out, or_8_out, or_9_out;

  or or_1 (or_1_out, M179, M178, M177, M176, M175);
  or or_2 (or_2_out, M174, M173, M172, M171, M170);
  or or_3 (or_3_out, M179, M178, M177, M176, M175, M168, M162, M161, M160, M159, M158, M151, M145, M144, M143, M142, M141, M134, M128, M127, M126, M125);
  or or_4 (or_4_out, M124, M117, M111, M110, M109, M108, M107, M100, M94, M93, M92, M91, M90, M83, M77, M76, M75, M74, M73, M66, M60, M59);
  or or_5 (or_5_out, M58, M57, M56, M49, M43, M42, M41, M40, M39, M32, M26, M25, M24, M23, M22, M15, M9, M8, M7, M6, M5);
  or or_6 (or_6_out, M174, M173, M172, M171, M170, M157, M156, M155, M154, M153, M140, M139, M138, M137, M136, M123, M122, M121, M120, M119, M106, M105, M104, M103, M102, M89, M88, M87);
  or or_7 (or_7_out, M86, M85, M72, M71, M70, M69, M68, M55, M54, M53, M52, M51, M38, M37, M36, M35, M34, M21, M20, M19, M18, M17, M4, M3, M2, M1, M0);
  and and_1 (and_1_out, or_1_out, T4);
  and and_2 (and_2_out, T5, or_2_out);
  or or_8 (or_8_out, or_3_out, or_4_out, or_5_out);
  and and_3 (and_3_out, or_8_out, T3);
  or or_9 (or_9_out, or_6_out, or_7_out);
  and and_4 (and_4_out, or_9_out, T4);
  or or_10 (DR_BUS, and_1_out, and_2_out);
  or or_11 (DR_LOAD, and_3_out, and_4_out);
endmodule

module AX (
  input  C,
  input  Z,
  input  T3,
  input  T4,
  input  T5,
  input  E0,
  input  E1,
  input  E2,
  input  E3,
  input  E4,
  input  E20,
  input  E21,
  input  E22,
  input  E23,
  input  E24,
  input  M0,
  input  M5,
  input  M10,
  input  M15,
  input  M16,
  input  M17,
  input  M22,
  input  M27,
  input  M32,
  input  M33,
  input  M34,
  input  M39,
  input  M44,
  input  M49,
  input  M50,
  input  M51,
  input  M56,
  input  M61,
  input  M66,
  input  M67,
  input  M68,
  input  M73,
  input  M78,
  input  M83,
  input  M84,
  input  M85,
  input  M90,
  input  M95,
  input  M100,
  input  M101,
  input  M102,
  input  M107,
  input  M112,
  input  M117,
  input  M118,
  input  M119,
  input  M123,
  input  M124,
  input  M128,
  input  M129,
  input  M133,
  input  M134,
  input  M135,
  input  M136,
  input  M140,
  input  M141,
  input  M145,
  input  M146,
  input  M150,
  input  M151,
  input  M152,
  input  M170,
  input  M175,
  input  M180,
  input  M185,
  input  M190,
  input  M195,
  input  M198,
  input  M201,
  input  M204,
  input  M207,
  input  M210,
  input  M213,
  input  M214,
  input  M215,
  input  M216,
  input  M217,
  input  M218,
  input  M219,
  input  M220,
  input  M221,
  output AX_INC,
  output AX_DEC,
  output AX_SHL,
  output AX_SHR,
  output AX_CIL,
  output AX_CIR,
  output AX_CML,
  output AX_CLR,
  output AX_LOAD,
  output AX_BUS
);

  wire and_9_out, and_10_out, and_11_out, and_12_out, and_13_out, and_14_out, and_15_out, and_16_out,
       and_17_out, and_18_out, and_19_out, and_20_out, and_21_out, and_22_out, and_23_out, and_24_out,
       or_1_out, or_2_out, or_3_out, or_4_out, or_5_out, or_6_out, or_7_out, or_8_out, or_9_out, or_10_out,
       or_11_out, or_12_out, or_13_out, or_14_out;

  and and_1 (AX_INC, M220, E0, T3);
  and and_2 (AX_DEC, M221, E0, T3);
  and and_3 (AX_SHL, M216, E0, T3);
  and and_4 (AX_SHR, M217, E0, T3);
  and and_5 (AX_CIL, M218, E0, T3);
  and and_6 (AX_CIR, M219, E0, T3);
  and and_7 (AX_CML, M215, E0, T3);
  and and_8 (AX_CLR, M214, E0, T3);
  or or_1 (or_1_out, E4, E3, E2, E1, E0);
  or or_2 (or_2_out, M118, M101, M84, M67, M50, M33, M16);
  or or_3 (or_3_out, M152, M135);
  or or_4 (or_4_out, E3, E2, E1, E0);
  or or_5 (or_5_out, M190, M150, M146, M133, M129, M112, M95, M78, M61, M44, M27, M10);
  or or_6 (or_6_out, M117, M100, M83, M66, M49, M32, M15);
  or or_7 (or_7_out, M175, M145, M141, M128, M124, M107, M90, M73, M56, M39, M22, M5);
  or or_8 (or_8_out, M170, M140, M136, M123, M119, M102, M85, M68, M51, M34, M17, M0);
  and and_9 (and_9_out, M180, T4);
  and and_10 (and_10_out, M201, Z);
  and and_11 (and_11_out, M204, ~Z);  // AND_Gate
  and and_12 (and_12_out, M207, C, ~Z);  // AND_Gate
  and and_13 (and_13_out, M210, ~C, Z);  // AND_Gate
  and and_14 (and_14_out, M213, C, Z);
  or or_9 (or_9_out, or_1_out, E24, E23, E22, E21, E20);
  and and_15 (and_15_out, or_4_out, M195);
  and and_16 (and_16_out, or_1_out, or_6_out);
  or or_10 (or_10_out, M151, M134);
  and and_17 (and_17_out, or_8_out, T5);
  and and_18 (and_18_out, or_1_out, or_2_out);
  and and_19 (and_19_out, or_9_out, or_3_out);
  and and_20 (and_20_out, or_9_out, or_10_out);
  or or_11 (or_11_out, M198, and_10_out, and_11_out, and_12_out, and_13_out, and_14_out);
  and and_21 (and_21_out, or_11_out, E0);
  or or_12 (or_12_out, and_18_out, and_19_out, and_15_out, or_5_out);
  or or_13 (or_13_out, and_16_out, and_20_out, or_7_out);
  or or_14 (or_14_out, M185, and_21_out);
  and and_22 (and_22_out, or_14_out, T3);
  and and_23 (and_23_out, or_12_out, T3);
  and and_24 (and_24_out, or_13_out, T4);
  or or_15 (AX_BUS, and_9_out, and_22_out);
  or or_16 (AX_LOAD, and_23_out, and_24_out, and_17_out);
endmodule

module BX (
  input  C,
  input  Z,
  input  T3,
  input  T4,
  input  T5,
  input  E0,
  input  E1,
  input  E2,
  input  E3,
  input  E4,
  input  E5,
  input  E6,
  input  E7,
  input  E8,
  input  E9,
  input  M1,
  input  M6,
  input  M11,
  input  M15,
  input  M16,
  input  M18,
  input  M23,
  input  M28,
  input  M32,
  input  M33,
  input  M35,
  input  M40,
  input  M45,
  input  M49,
  input  M50,
  input  M52,
  input  M57,
  input  M62,
  input  M66,
  input  M67,
  input  M69,
  input  M74,
  input  M79,
  input  M83,
  input  M84,
  input  M86,
  input  M91,
  input  M96,
  input  M100,
  input  M101,
  input  M103,
  input  M108,
  input  M113,
  input  M117,
  input  M118,
  input  M119,
  input  M120,
  input  M124,
  input  M125,
  input  M129,
  input  M130,
  input  M134,
  input  M135,
  input  M136,
  input  M137,
  input  M141,
  input  M142,
  input  M146,
  input  M147,
  input  M151,
  input  M152,
  input  M171,
  input  M176,
  input  M181,
  input  M186,
  input  M191,
  input  M195,
  input  M198,
  input  M201,
  input  M204,
  input  M207,
  input  M210,
  input  M213,
  input  M214,
  input  M215,
  input  M216,
  input  M217,
  input  M218,
  input  M219,
  input  M220,
  input  M221,
  output BX_INC,
  output BX_DEC,
  output BX_SHL,
  output BX_SHR,
  output BX_CIL,
  output BX_CIR,
  output BX_CML,
  output BX_CLR,
  output BX_LOAD,
  output BX_BUS
);

  wire and_9_out, and_10_out, and_11_out, and_12_out, and_13_out, and_14_out, and_15_out, and_16_out,
       and_17_out, and_18_out, and_19_out, and_20_out, and_21_out, and_22_out, and_23_out, and_24_out,
       or_1_out, or_2_out, or_3_out, or_4_out, or_5_out, or_6_out, or_7_out, or_8_out, or_9_out, or_10_out,
       or_12_out;

  and and_1 (BX_INC, M220, E1, T3);
  and and_2 (BX_DEC, M221, E1, T3);
  and and_3 (BX_SHL, M216, E1, T3);
  and and_4 (BX_SHR, M217, E1, T3);
  and and_5 (BX_CIL, M218, E1, T3);
  and and_6 (BX_CIR, M219, E1, T3);
  and and_7 (BX_CML, M215, E1, T3);
  and and_8 (BX_CLR, M214, E1, T3);
  or or_1 (or_1_out, E9, E8, E7, E6, E5);
  or or_2 (or_2_out, M118, M101, M84, M67, M50, M33, M16);
  or or_3 (or_3_out, M152, M135);
  or or_4 (or_4_out, E7, E6, E5, E4);
  or or_5 (or_5_out, M151, M134);
  and and_9 (and_9_out, M181, T4);
  and and_10 (and_10_out, M198, E1);
  and and_11 (and_11_out, M201, E1, Z);
  and and_12 (and_12_out, M204, E1, ~Z);  // AND_Gate
  and and_13 (and_13_out, M207, E1, ~Z, C);  // AND_Gate
  and and_14 (and_14_out, M210, E1, Z, ~C);  // AND_Gate
  and and_15 (and_15_out, M213, E1, Z, C);
  or or_6 (or_6_out, or_1_out, E4, E3, E2, E1, E0);
  or or_7 (or_7_out, M117, M100, M83, M66, M49, M32, M15);
  or or_8 (or_8_out, M171, M137, M136, M120, M119, M103, M86, M69, M52, M35, M18, M1);
  and and_16 (and_16_out, or_8_out, T5);
  and and_17 (and_17_out, or_1_out, or_2_out);
  and and_18 (and_18_out, or_6_out, or_3_out);
  and and_19 (and_19_out, M195, or_4_out);
  and and_20 (and_20_out, or_1_out, or_7_out);
  and and_21 (and_21_out, or_6_out, or_5_out);
  or or_9 (or_9_out, M186, and_10_out, and_11_out, and_12_out, and_13_out, and_14_out, and_15_out);
  and and_22 (and_22_out, or_9_out, T3);
  or or_10 (or_10_out, and_17_out, and_18_out, and_19_out, M191, M147, M146, M130, M129, M113, M96, M79, M62, M45, M28, M11);
  or or_11 (BX_BUS, and_9_out, and_22_out);
  and and_23 (and_23_out, or_10_out, T3);
  or or_12 (or_12_out, and_20_out, and_21_out, M176, M142, M141, M125, M124, M108, M91, M74, M57, M40, M23, M6);
  and and_24 (and_24_out, or_12_out, T4);
  or or_13 (BX_LOAD, and_23_out, and_24_out, and_16_out);
endmodule

module CX (
  input  C,
  input  Z,
  input  T3,
  input  T4,
  input  T5,
  input  E2,
  input  E5,
  input  E6,
  input  E7,
  input  E8,
  input  E9,
  input  E10,
  input  E11,
  input  E12,
  input  E13,
  input  E14,
  input  M2,
  input  M7,
  input  M12,
  input  M15,
  input  M16,
  input  M19,
  input  M24,
  input  M29,
  input  M32,
  input  M33,
  input  M36,
  input  M41,
  input  M46,
  input  M49,
  input  M50,
  input  M53,
  input  M58,
  input  M63,
  input  M66,
  input  M67,
  input  M70,
  input  M75,
  input  M80,
  input  M83,
  input  M84,
  input  M87,
  input  M92,
  input  M97,
  input  M100,
  input  M101,
  input  M104,
  input  M109,
  input  M114,
  input  M117,
  input  M118,
  input  M120,
  input  M121,
  input  M125,
  input  M126,
  input  M130,
  input  M131,
  input  M134,
  input  M135,
  input  M137,
  input  M138,
  input  M142,
  input  M143,
  input  M147,
  input  M148,
  input  M151,
  input  M152,
  input  M172,
  input  M177,
  input  M182,
  input  M187,
  input  M192,
  input  M195,
  input  M198,
  input  M201,
  input  M204,
  input  M207,
  input  M210,
  input  M213,
  input  M214,
  input  M215,
  input  M216,
  input  M217,
  input  M218,
  input  M219,
  input  M220,
  input  M221,
  output CX_INC,
  output CX_DEC,
  output CX_SHL,
  output CX_SHR,
  output CX_CIL,
  output CX_CIR,
  output CX_CML,
  output CX_CLR,
  output CX_LOAD,
  output CX_BUS
);

  wire and_9_out, and_10_out, and_11_out, and_12_out, and_13_out, and_14_out, and_15_out, and_16_out,
       and_17_out, and_18_out, and_19_out, and_20_out, and_21_out, and_22_out, and_23_out, and_24_out,
       or_1_out, or_2_out, or_3_out, or_4_out, or_5_out, or_6_out, or_7_out, or_8_out, or_9_out, or_10_out,
       or_11_out, or_12_out, or_14_out;

  and and_1 (CX_INC, M220, E2, T3);
  and and_2 (CX_DEC, M221, E2, T3);
  and and_3 (CX_SHL, M216, E2, T3);
  and and_4 (CX_SHR, M217, E2, T3);
  and and_5 (CX_CIL, M218, E2, T3);
  and and_6 (CX_CIR, M219, E2, T3);
  and and_7 (CX_CML, M215, E2, T3);
  and and_8 (CX_CLR, M214, E2, T3);
  or or_1 (or_1_out, E14, E13, E12, E11, E10);
  or or_2 (or_2_out, M118, M101, M84, M67, M50, M33, M16);
  or or_3 (or_3_out, M152, M135);
  or or_4 (or_4_out, E11, E10, E9, E8);
  or or_5 (or_5_out, M192, M148, M147, M131, M130, M114, M97, M80, M63, M46, M29, M12);
  or or_6 (or_6_out, M117, M100, M83, M66, M49, M32, M15);
  or or_7 (or_7_out, M151, M134);
  or or_8 (or_8_out, M177, M143, M142, M126, M125, M109, M92, M75, M58, M41, M24, M7);
  or or_9 (or_9_out, M172, M138, M137, M121, M120, M104, M87, M70, M53, M36, M19, M2);
  and and_9 (and_9_out, M182, T4);
  and and_10 (and_10_out, M198, E2);
  and and_11 (and_11_out, M201, E2, Z);
  and and_12 (and_12_out, M204, E2, ~Z);  // AND_Gate
  and and_13 (and_13_out, M207, E2, ~Z, C);  // AND_Gate
  and and_14 (and_14_out, M210, E2, Z, ~C);  // AND_Gate
  and and_15 (and_15_out, M213, E2, Z, C);
  or or_10 (or_10_out, or_1_out, E9, E8, E7, E6, E5);
  and and_16 (and_16_out, or_4_out, M195);
  and and_17 (and_17_out, or_1_out, or_6_out);
  and and_18 (and_18_out, or_9_out, T5);
  or or_11 (or_11_out, M187, and_10_out, and_11_out, and_12_out, and_13_out, and_14_out, and_15_out);
  and and_19 (and_19_out, or_1_out, or_2_out);
  and and_20 (and_20_out, or_10_out, or_3_out);
  and and_21 (and_21_out, or_10_out, or_7_out);
  and and_22 (and_22_out, or_11_out, T3);
  or or_12 (or_12_out, and_17_out, and_21_out, or_8_out);
  or or_13 (CX_BUS, and_9_out, and_22_out);
  or or_14 (or_14_out, and_19_out, and_20_out, and_16_out, or_5_out);
  and and_23 (and_23_out, or_12_out, T4);
  and and_24 (and_24_out, or_14_out, T3);
  or or_15 (CX_LOAD, and_24_out, and_23_out, and_18_out);
endmodule

module DX (
  input  C,
  input  Z,
  input  T3,
  input  T4,
  input  T5,
  input  E3,
  input  E10,
  input  E11,
  input  E12,
  input  E13,
  input  E14,
  input  E15,
  input  E16,
  input  E17,
  input  E18,
  input  E19,
  input  M3,
  input  M8,
  input  M13,
  input  M15,
  input  M16,
  input  M20,
  input  M25,
  input  M30,
  input  M32,
  input  M33,
  input  M37,
  input  M42,
  input  M47,
  input  M49,
  input  M50,
  input  M54,
  input  M59,
  input  M64,
  input  M66,
  input  M67,
  input  M71,
  input  M76,
  input  M81,
  input  M83,
  input  M84,
  input  M88,
  input  M93,
  input  M98,
  input  M100,
  input  M101,
  input  M105,
  input  M110,
  input  M115,
  input  M117,
  input  M118,
  input  M121,
  input  M122,
  input  M126,
  input  M127,
  input  M131,
  input  M132,
  input  M134,
  input  M135,
  input  M138,
  input  M139,
  input  M143,
  input  M144,
  input  M148,
  input  M149,
  input  M151,
  input  M152,
  input  M173,
  input  M178,
  input  M183,
  input  M188,
  input  M193,
  input  M195,
  input  M198,
  input  M201,
  input  M204,
  input  M207,
  input  M210,
  input  M213,
  input  M214,
  input  M215,
  input  M216,
  input  M217,
  input  M218,
  input  M219,
  input  M220,
  input  M221,
  output DX_INC,
  output DX_DEC,
  output CX_SHL,
  output DX_SHR,
  output DX_CIL,
  output DX_CIR,
  output DX_CML,
  output DX_CLR,
  output DX_LOAD,
  output DX_BUS
);

  wire and_9_out, and_10_out, and_11_out, and_12_out, and_13_out, and_14_out, and_15_out, and_16_out,
       and_17_out, and_18_out, and_19_out, and_20_out, and_21_out, and_22_out, and_23_out, and_24_out,
       or_1_out, or_2_out, or_3_out, or_4_out, or_5_out, or_6_out, or_7_out, or_8_out, or_9_out, or_10_out,
       or_11_out, or_12_out, or_14_out;

  and and_1 (DX_INC, M220, E3, T3);
  and and_2 (DX_DEC, M221, E3, T3);
  and and_3 (CX_SHL, M216, E3, T3);
  and and_4 (DX_SHR, M217, E3, T3);
  and and_5 (DX_CIL, M218, E3, T3);
  and and_6 (DX_CIR, M219, E3, T3);
  and and_7 (DX_CML, M215, E3, T3);
  and and_8 (DX_CLR, M214, E3, T3);
  or or_1 (or_1_out, E19, E18, E17, E16, E15);
  or or_2 (or_2_out, M118, M101, M84, M67, M50, M33, M16);
  or or_3 (or_3_out, M152, M135);
  or or_4 (or_4_out, E15, E14, E13, E12);
  or or_5 (or_5_out, M193, M149, M148, M132, M131, M115, M98, M81, M64, M47, M30, M13);
  or or_6 (or_6_out, M117, M100, M83, M66, M49, M32, M15);
  or or_7 (or_7_out, M151, M134);
  or or_8 (or_8_out, M178, M144, M143, M127, M126, M110, M93, M76, M59, M42, M25, M8);
  or or_9 (or_9_out, M173, M139, M138, M122, M121, M105, M88, M71, M54, M37, M20, M3);
  and and_9 (and_9_out, M183, T4);
  and and_10 (and_10_out, M198, E3);
  and and_11 (and_11_out, M201, E3, Z);
  and and_12 (and_12_out, M204, E3, ~Z);  // AND_Gate
  and and_13 (and_13_out, M207, E3, ~Z, C);  // AND_Gate
  and and_14 (and_14_out, M210, E3, Z, ~C);  // AND_Gate
  and and_15 (and_15_out, M213, E3, Z, C);
  and and_16 (and_16_out, or_1_out, or_6_out);
  and and_17 (and_17_out, or_9_out, T5);
  or or_10 (or_10_out, M188, and_10_out, and_11_out, and_12_out, and_13_out, and_14_out, and_15_out);
  and and_18 (and_18_out, or_1_out, or_2_out);
  or or_11 (or_11_out, or_1_out, E14, E13, E12, E11, E10);
  and and_19 (and_19_out, or_11_out, or_3_out);
  and and_20 (and_20_out, or_4_out, M195);
  and and_21 (and_21_out, or_11_out, or_7_out);
  and and_22 (and_22_out, or_10_out, T3);
  or or_12 (or_12_out, and_16_out, and_21_out, or_8_out);
  or or_13 (DX_BUS, and_9_out, and_22_out);
  or or_14 (or_14_out, and_18_out, and_19_out, and_20_out, or_5_out);
  and and_23 (and_23_out, or_12_out, T4);
  and and_24 (and_24_out, or_14_out, T3);
  or or_15 (DX_LOAD, and_24_out, and_23_out, and_17_out);
endmodule

module EX (
  input  C,
  input  Z,
  input  T3,
  input  T4,
  input  T5,
  input  E4,
  input  E15,
  input  E16,
  input  E17,
  input  E18,
  input  E19,
  input  E20,
  input  E21,
  input  E22,
  input  E23,
  input  E24,
  input  M4,
  input  M9,
  input  M14,
  input  M15,
  input  M16,
  input  M21,
  input  M26,
  input  M31,
  input  M32,
  input  M33,
  input  M38,
  input  M43,
  input  M48,
  input  M49,
  input  M50,
  input  M55,
  input  M60,
  input  M65,
  input  M66,
  input  M67,
  input  M72,
  input  M77,
  input  M82,
  input  M83,
  input  M84,
  input  M89,
  input  M94,
  input  M99,
  input  M100,
  input  M101,
  input  M106,
  input  M111,
  input  M116,
  input  M117,
  input  M118,
  input  M122,
  input  M123,
  input  M127,
  input  M128,
  input  M132,
  input  M133,
  input  M134,
  input  M135,
  input  M139,
  input  M140,
  input  M144,
  input  M145,
  input  M149,
  input  M150,
  input  M151,
  input  M152,
  input  M174,
  input  M179,
  input  M184,
  input  M189,
  input  M194,
  input  M195,
  input  M198,
  input  M201,
  input  M204,
  input  M207,
  input  M210,
  input  M213,
  input  M214,
  input  M215,
  input  M216,
  input  M217,
  input  M218,
  input  M219,
  input  M220,
  input  M221,
  output EX_INC,
  output EX_DEC,
  output EX_SHL,
  output EX_SHR,
  output EX_CIL,
  output EX_CIR,
  output EX_CML,
  output EX_CLR,
  output EX_LOAD,
  output EX_BUS
);

  wire and_9_out, and_10_out, and_11_out, and_12_out, and_13_out, and_14_out, and_15_out, and_16_out,
       and_17_out, and_18_out, and_19_out, and_20_out, and_21_out, and_22_out, and_23_out, and_24_out,
       or_1_out, or_2_out, or_3_out, or_4_out, or_5_out, or_6_out, or_7_out, or_8_out, or_9_out, or_10_out,
       or_11_out, or_12_out, or_14_out;

  and and_1 (EX_INC, M220, E4, T3);
  and and_2 (EX_DEC, M221, E4, T3);
  and and_3 (EX_SHL, M216, E4, T3);
  and and_4 (EX_SHR, M217, E4, T3);
  and and_5 (EX_CIL, M218, E4, T3);
  and and_6 (EX_CIR, M219, E4, T3);
  and and_7 (EX_CML, M215, E4, T3);
  and and_8 (EX_CLR, M214, E4, T3);
  or or_1 (or_1_out, E24, E23, E22, E21, E20);
  or or_2 (or_2_out, M118, M101, M84, M67, M50, M33, M16);
  or or_3 (or_3_out, M152, M135);
  or or_4 (or_4_out, E19, E18, E17, E16);
  or or_5 (or_5_out, M194, M150, M149, M133, M132, M116, M99, M82, M65, M48, M31, M14);
  or or_6 (or_6_out, M117, M100, M83, M66, M49, M32, M15);
  or or_7 (or_7_out, M151, M134);
  or or_8 (or_8_out, M179, M145, M144, M128, M127, M111, M94, M77, M60, M43, M26, M9);
  or or_9 (or_9_out, M174, M140, M139, M123, M122, M106, M89, M72, M55, M38, M21, M4);
  and and_9 (and_9_out, M184, T4);
  and and_10 (and_10_out, M198, E4);
  and and_11 (and_11_out, M201, E4, Z);
  and and_12 (and_12_out, M204, E4, ~Z);  // AND_Gate
  and and_13 (and_13_out, M207, E4, ~Z, C);  // AND_Gate
  and and_14 (and_14_out, M210, E4, Z, ~C);  // AND_Gate
  and and_15 (and_15_out, M213, E4, Z, C);
  and and_16 (and_16_out, or_1_out, or_6_out);
  and and_17 (and_17_out, or_9_out, T5);
  or or_10 (or_10_out, M189, and_10_out, and_11_out, and_12_out, and_13_out, and_14_out, and_15_out);
  and and_18 (and_18_out, or_1_out, or_2_out);
  or or_11 (or_11_out, or_1_out, E19, E18, E17, E16, E15);
  and and_19 (and_19_out, or_11_out, or_3_out);
  and and_20 (and_20_out, or_4_out, M195);
  and and_21 (and_21_out, or_11_out, or_7_out);
  and and_22 (and_22_out, or_10_out, T3);
  or or_12 (or_12_out, and_16_out, and_21_out, or_8_out);
  or or_13 (EX_BUS, and_9_out, and_22_out);
  or or_14 (or_14_out, and_18_out, and_19_out, and_20_out, or_5_out);
  and and_23 (and_23_out, or_12_out, T4);
  and and_24 (and_24_out, or_14_out, T3);
  or or_15 (EX_LOAD, and_24_out, and_23_out, and_17_out);
endmodule

module MEMORY (
  input  T3,
  input  T4,
  input  E0,
  input  E1,
  input  E2,
  input  E3,
  input  E4,
  input  E5,
  input  E6,
  input  E7,
  input  E8,
  input  E9,
  input  E10,
  input  E11,
  input  E12,
  input  E13,
  input  E14,
  input  E15,
  input  E16,
  input  E17,
  input  E18,
  input  E19,
  input  E20,
  input  E21,
  input  E22,
  input  E23,
  input  E24,
  input  M0,
  input  M1,
  input  M2,
  input  M3,
  input  M4,
  input  M5,
  input  M6,
  input  M7,
  input  M8,
  input  M9,
  input  M15,
  input  M17,
  input  M18,
  input  M19,
  input  M20,
  input  M21,
  input  M22,
  input  M23,
  input  M24,
  input  M25,
  input  M26,
  input  M32,
  input  M34,
  input  M35,
  input  M36,
  input  M37,
  input  M38,
  input  M39,
  input  M40,
  input  M41,
  input  M42,
  input  M43,
  input  M49,
  input  M51,
  input  M52,
  input  M53,
  input  M54,
  input  M55,
  input  M56,
  input  M57,
  input  M58,
  input  M59,
  input  M60,
  input  M66,
  input  M68,
  input  M69,
  input  M70,
  input  M71,
  input  M72,
  input  M73,
  input  M74,
  input  M75,
  input  M76,
  input  M77,
  input  M83,
  input  M85,
  input  M86,
  input  M87,
  input  M88,
  input  M89,
  input  M90,
  input  M91,
  input  M92,
  input  M93,
  input  M94,
  input  M100,
  input  M102,
  input  M103,
  input  M104,
  input  M105,
  input  M106,
  input  M107,
  input  M108,
  input  M109,
  input  M110,
  input  M111,
  input  M117,
  input  M119,
  input  M120,
  input  M121,
  input  M122,
  input  M123,
  input  M124,
  input  M125,
  input  M126,
  input  M127,
  input  M128,
  input  M134,
  input  M136,
  input  M137,
  input  M138,
  input  M139,
  input  M140,
  input  M141,
  input  M142,
  input  M143,
  input  M144,
  input  M145,
  input  M151,
  input  M153,
  input  M154,
  input  M155,
  input  M156,
  input  M157,
  input  M158,
  input  M159,
  input  M160,
  input  M161,
  input  M162,
  input  M168,
  input  M170,
  input  M171,
  input  M172,
  input  M173,
  input  M174,
  input  M175,
  input  M176,
  input  M177,
  input  M178,
  input  M179,
  input  M180,
  input  M181,
  input  M182,
  input  M183,
  input  M184,
  input  M185,
  input  M186,
  input  M187,
  input  M188,
  input  M189,
  input  M196,
  input  M199,
  input  M202,
  input  M205,
  input  M208,
  input  M211,
  output STR,
  output BUS,
  output [2:0] MUX
);

  wire and_1_out, and_2_out, and_3_out, and_4_out, and_5_out, and_6_out, and_7_out, and_8_out, and_9_out,
       and_10_out, and_11_out, and_12_out, or_1_out, or_2_out, or_3_out, or_4_out, or_5_out, or_6_out,
       or_7_out, or_8_out, or_9_out, or_10_out, or_11_out, or_12_out, or_13_out, or_14_out, or_15_out,
       or_16_out, or_17_out, or_18_out, or_19_out, or_20_out, or_21_out, or_22_out, or_23_out, or_24_out,
       or_25_out, or_27_out, or_28_out;

  or or_1 (or_1_out, M189, M188, M187, M186, M185);
  or or_2 (or_2_out, M184, M183, M182, M181, M180);
  or or_3 (or_3_out, E24, E23, E22, E21, E20, E19, E18, E17, E16, E15, E14, E13, E12, E11, E10, E9, E8, E7, E6, E5, E4, E3, E2, E1, E0);
  or or_4 (or_4_out, M168, M151, M134, M117, M100, M83, M66, M49, M32, M15);
  or or_5 (or_5_out, M211, M208, M205, M202, M199, M196, M184, M183, M182, M181, M180, M179, M178, M177, M176, M175, M174, M173, M172, M171, M170, M162, M161, M160, M159, M158, M157, M156, M155, M154, M153, M145);
  or or_6 (or_6_out, or_5_out, M144, M143, M142, M141, M140, M139, M138, M137, M136, M128, M127, M126, M125, M124, M123, M122, M121, M120, M119, M111, M110, M109, M108, M107, M106, M105, M104, M103, M102, M94, M93);
  or or_7 (or_7_out, or_6_out, M92, M91, M90, M89, M88, M87, M86, M85, M77, M76, M75, M74, M73, M72, M71, M70, M69, M68, M60, M59, M58, M57, M56, M55, M54, M53, M52, M51, M43, M42, M41);
  or or_8 (or_8_out, or_7_out, M40, M39, M38, M37, M36, M35, M34, M26, M25, M24, M23, M22, M21, M20, M19, M18, M17, M9, M8, M7, M6, M5, M4, M3, M2, M1, M0);
  or or_9 (or_9_out, M174, M173, M172, M171, M170, M157, M156, M155, M154, M153, M140, M139, M138, M137, M136, M123, M122, M121, M120, M119, M106, M105);
  or or_10 (or_10_out, or_9_out, M104, M103, M102, M89, M88, M87, M86, M85, M72, M71, M70, M69, M68, M55, M54, M53, M52, M51, M38, M37, M36);
  or or_11 (or_11_out, or_10_out, M35, M34, M21, M20, M19, M18, M17, M4, M3, M2, M1, M0);
  or or_12 (or_12_out, M211, M208, M205, M202, M199, M196, M189, M188, M187, M186, M185, M184, M183, M182, M181, M180, M179, M178, M177, M176, M175, M174);
  or or_13 (or_13_out, or_12_out, M173, M172, M171, M170, M162, M161, M160, M159, M158, M157, M156, M155, M154, M153, M145, M144, M143, M142, M141, M140, M139);
  or or_14 (or_14_out, or_13_out, M138, M137, M136, M128, M127, M126, M125, M124, M123, M122, M121, M120, M119, M111, M110, M109, M108, M107, M106, M105, M104);
  or or_15 (or_15_out, or_14_out, M103, M102, M94, M93, M92, M91, M90, M89, M88, M87, M86, M85, M77, M76, M75, M74, M73, M72, M71, M70, M69);
  or or_16 (or_16_out, or_15_out, M68, M60, M59, M58, M57, M56, M55, M54, M53, M52, M51, M43, M42, M41, M40, M39, M38, M37, M36, M35, M34);
  or or_17 (or_17_out, or_16_out, M26, M25, M24, M23, M22, M21, M20, M19, M18, M17, M9, M8, M7, M6, M5, M4, M3, M2, M1, M0);
  or or_18 (or_18_out, M184, M183, M182, M181, M180, M174, M173, M172, M171, M170, M157, M156, M155, M154, M153, M140, M139, M138, M137, M136, M123, M122, M121, M120, M119, M106, M105, M104, M103, M102, M89, M88);
  or or_19 (or_19_out, or_18_out, M87, M86, M85, M72, M71, M70, M69, M68, M55, M54, M53, M52, M51, M38, M37, M36, M35, M34, M21, M20, M19, M18, M17, M4, M3, M2, M1, M0);
  or or_20 (or_20_out, E20, E15, E10, E5, E0);
  or or_21 (or_21_out, E21, E16, E11, E6, E1);
  or or_22 (or_22_out, E22, E17, E12, E7, E2);
  or or_23 (or_23_out, E23, E18, E13, E8, E3);
  or or_24 (or_24_out, E24, E19, E14, E9, E4);
  and and_1 (and_1_out, or_1_out, T3);
  and and_2 (and_2_out, T4, or_2_out);
  and and_3 (and_3_out, or_11_out, T4);
  or or_25 (or_25_out, M168, M151, M134, M117, M100, M83, M66, M49, M32, M15);
  or or_26 (STR, and_1_out, and_2_out);
  and and_4 (and_4_out, or_3_out, or_4_out);
  and and_5 (and_5_out, or_17_out, T3);
  and and_6 (and_6_out, or_19_out, T4);
  or or_27 (or_27_out, and_4_out, or_8_out);
  and and_7 (and_7_out, or_27_out, T3);
  or or_28 (or_28_out, and_5_out, and_6_out);
  and and_8 (and_8_out, or_25_out, or_20_out, T3);
  and and_9 (and_9_out, or_25_out, or_21_out, T3);
  and and_10 (and_10_out, or_25_out, or_22_out, T3);
  and and_11 (and_11_out, or_25_out, or_23_out, T3);
  and and_12 (and_12_out, or_25_out, or_24_out, T3);
  or or_29 (BUS, and_7_out, and_3_out);
  assign MUX = or_28_out ? 3'b000 : 3'bz;  // Controlled_Buffer controlled_buffer_1
  assign MUX = and_8_out ? 3'b001 : 3'bz;  // Controlled_Buffer controlled_buffer_2
  assign MUX = and_9_out ? 3'b010 : 3'bz;  // Controlled_Buffer controlled_buffer_3
  assign MUX = and_10_out ? 3'b011 : 3'bz;  // Controlled_Buffer controlled_buffer_4
  assign MUX = and_11_out ? 3'b100 : 3'bz;  // Controlled_Buffer controlled_buffer_5
  assign MUX = and_12_out ? 3'b101 : 3'bz;  // Controlled_Buffer controlled_buffer_6
endmodule

module FIRST_REGISTER (
  input  T3,
  input  T4,
  input  T5,
  input  E0,
  input  E1,
  input  E2,
  input  E3,
  input  E4,
  input  E5,
  input  E6,
  input  E7,
  input  E8,
  input  E9,
  input  E10,
  input  E11,
  input  E12,
  input  E13,
  input  E14,
  input  E15,
  input  E16,
  input  E17,
  input  E18,
  input  E19,
  input  E20,
  input  E21,
  input  E22,
  input  E23,
  input  E24,
  input  M0,
  input  M1,
  input  M2,
  input  M3,
  input  M4,
  input  M5,
  input  M6,
  input  M7,
  input  M8,
  input  M9,
  input  M10,
  input  M11,
  input  M12,
  input  M13,
  input  M14,
  input  M15,
  input  M16,
  input  M17,
  input  M18,
  input  M19,
  input  M20,
  input  M21,
  input  M22,
  input  M23,
  input  M24,
  input  M25,
  input  M26,
  input  M27,
  input  M28,
  input  M29,
  input  M30,
  input  M31,
  input  M32,
  input  M33,
  input  M34,
  input  M35,
  input  M36,
  input  M37,
  input  M38,
  input  M39,
  input  M40,
  input  M41,
  input  M42,
  input  M43,
  input  M44,
  input  M45,
  input  M46,
  input  M47,
  input  M48,
  input  M49,
  input  M50,
  input  M51,
  input  M52,
  input  M53,
  input  M54,
  input  M55,
  input  M56,
  input  M57,
  input  M58,
  input  M59,
  input  M60,
  input  M61,
  input  M62,
  input  M63,
  input  M64,
  input  M65,
  input  M66,
  input  M67,
  input  M68,
  input  M69,
  input  M70,
  input  M71,
  input  M72,
  input  M73,
  input  M74,
  input  M75,
  input  M76,
  input  M77,
  input  M78,
  input  M79,
  input  M80,
  input  M81,
  input  M82,
  input  M83,
  input  M84,
  input  M85,
  input  M86,
  input  M87,
  input  M88,
  input  M89,
  input  M90,
  input  M91,
  input  M92,
  input  M93,
  input  M94,
  input  M95,
  input  M96,
  input  M97,
  input  M98,
  input  M99,
  input  M100,
  input  M101,
  input  M102,
  input  M103,
  input  M104,
  input  M105,
  input  M106,
  input  M107,
  input  M108,
  input  M109,
  input  M110,
  input  M111,
  input  M112,
  input  M113,
  input  M114,
  input  M115,
  input  M116,
  input  M117,
  input  M118,
  input  M119,
  input  M120,
  input  M121,
  input  M122,
  input  M123,
  input  M124,
  input  M125,
  input  M126,
  input  M127,
  input  M128,
  input  M129,
  input  M130,
  input  M131,
  input  M132,
  input  M133,
  input  M134,
  input  M135,
  input  M136,
  input  M137,
  input  M138,
  input  M139,
  input  M140,
  input  M141,
  input  M142,
  input  M143,
  input  M144,
  input  M145,
  input  M146,
  input  M147,
  input  M148,
  input  M149,
  input  M150,
  input  M151,
  input  M152,
  input  M153,
  input  M154,
  input  M155,
  input  M156,
  input  M157,
  input  M158,
  input  M159,
  input  M160,
  input  M161,
  input  M162,
  input  M163,
  input  M164,
  input  M165,
  input  M166,
  input  M167,
  input  M168,
  input  M169,
  input  M170,
  input  M171,
  input  M172,
  input  M173,
  input  M174,
  input  M175,
  input  M176,
  input  M177,
  input  M178,
  input  M179,
  input  M190,
  input  M191,
  input  M192,
  input  M193,
  input  M194,
  input  M195,
  output AX,
  output BX,
  output CX,
  output DX,
  output EX
);

  wire and_1_out, and_2_out, and_3_out, and_4_out, and_5_out, and_6_out, and_7_out, and_8_out, and_9_out,
       and_10_out, and_11_out, and_12_out, and_13_out, and_14_out, and_15_out, and_16_out, and_17_out,
       and_18_out, and_19_out, and_20_out, and_21_out, and_22_out, and_23_out, and_24_out, and_25_out,
       and_26_out, and_27_out, and_28_out, and_29_out, and_30_out, or_1_out, or_2_out, or_3_out, or_4_out,
       or_5_out, or_6_out, or_7_out, or_8_out, or_9_out, or_10_out, or_11_out, or_12_out, or_13_out,
       or_14_out, or_15_out, or_16_out, or_17_out, or_18_out, or_19_out, or_20_out, or_21_out, or_22_out,
       or_23_out, or_24_out, or_25_out, or_26_out, or_27_out, or_28_out, or_29_out, or_30_out, or_31_out,
       or_32_out, or_33_out, or_34_out, or_35_out, or_36_out, or_37_out, or_38_out, or_39_out, or_40_out,
       T3_out, T4_out;

  or u_T3 (T3_out, M152, M135, M118, M101, M84, M67, M50, M33, M16);
  or u_T4 (T4_out, M168, M151, M134, M117, M100, M83, M66, M49, M32, M15);
  or or_1 (or_1_out, E4, E3, E2, E1, E0);
  or or_2 (or_2_out, M190, M163, M146, M129, M112, M95, M78, M61, M44, M27, M10);
  or or_3 (or_3_out, E3, E2, E1, E0);
  or or_4 (or_4_out, M195, M169);
  or or_5 (or_5_out, M175, M158, M141, M124, M107, M90, M73, M56, M39, M22, M5);
  or or_6 (or_6_out, M170, M153, M136, M119, M102, M85, M68, M51, M34, M17, M0);
  or or_7 (or_7_out, E9, E8, E7, E6, E5);
  or or_8 (or_8_out, M191, M164, M147, M130, M113, M96, M79, M62, M45, M28, M11);
  or or_9 (or_9_out, E7, E6, E5, E4);
  or or_10 (or_10_out, M195, M169);
  or or_11 (or_11_out, M176, M159, M142, M125, M108, M91, M74, M57, M40, M23, M6);
  or or_12 (or_12_out, M171, M154, M137, M120, M103, M86, M69, M52, M35, M18, M1);
  or or_13 (or_13_out, E14, E13, E12, E11, E10);
  or or_14 (or_14_out, M192, M165, M148, M131, M114, M97, M80, M63, M46, M29, M12);
  or or_15 (or_15_out, E11, E10, E9, E8);
  or or_16 (or_16_out, M195, M169);
  or or_17 (or_17_out, M177, M160, M143, M126, M109, M92, M75, M58, M41, M24, M7);
  or or_18 (or_18_out, M172, M155, M138, M121, M104, M87, M70, M53, M36, M19, M2);
  or or_19 (or_19_out, E19, E18, E17, E16, E15);
  or or_20 (or_20_out, M193, M166, M149, M132, M115, M98, M81, M64, M47, M30, M13);
  or or_21 (or_21_out, E15, E14, E13, E12);
  or or_22 (or_22_out, M195, M169);
  or or_23 (or_23_out, M178, M161, M144, M127, M110, M93, M76, M59, M42, M25, M8);
  or or_24 (or_24_out, M173, M156, M139, M122, M105, M88, M71, M54, M37, M20, M3);
  or or_25 (or_25_out, E24, E23, E22, E21, E20);
  or or_26 (or_26_out, M194, M167, M150, M133, M116, M99, M82, M65, M48, M31, M14);
  or or_27 (or_27_out, E19, E18, E17, E16);
  or or_28 (or_28_out, M195, M169);
  or or_29 (or_29_out, M179, M162, M145, M128, M111, M94, M77, M60, M43, M26, M9);
  or or_30 (or_30_out, M174, M157, M140, M123, M106, M89, M72, M55, M38, M21, M4);
  and and_1 (and_1_out, or_1_out, T3_out);
  and and_2 (and_2_out, or_3_out, or_4_out);
  and and_3 (and_3_out, or_1_out, T4_out);
  and and_4 (and_4_out, or_6_out, T5);
  and and_5 (and_5_out, or_7_out, T3_out);
  and and_6 (and_6_out, or_9_out, or_10_out);
  and and_7 (and_7_out, or_7_out, T4_out);
  and and_8 (and_8_out, or_12_out, T5);
  and and_9 (and_9_out, or_13_out, T3_out);
  and and_10 (and_10_out, or_15_out, or_16_out);
  and and_11 (and_11_out, or_13_out, T4_out);
  and and_12 (and_12_out, or_18_out, T5);
  and and_13 (and_13_out, or_19_out, T3_out);
  and and_14 (and_14_out, or_21_out, or_22_out);
  and and_15 (and_15_out, or_19_out, T4_out);
  and and_16 (and_16_out, or_24_out, T5);
  and and_17 (and_17_out, or_25_out, T3_out);
  and and_18 (and_18_out, or_27_out, or_28_out);
  and and_19 (and_19_out, or_25_out, T4_out);
  and and_20 (and_20_out, or_30_out, T5);
  or or_31 (or_31_out, and_1_out, or_2_out, and_2_out);
  or or_32 (or_32_out, and_3_out, or_5_out);
  or or_33 (or_33_out, and_5_out, or_8_out, and_6_out);
  or or_34 (or_34_out, and_7_out, or_11_out);
  or or_35 (or_35_out, and_9_out, or_14_out, and_10_out);
  or or_36 (or_36_out, and_11_out, or_17_out);
  or or_37 (or_37_out, and_13_out, or_20_out, and_14_out);
  or or_38 (or_38_out, and_15_out, or_23_out);
  or or_39 (or_39_out, and_17_out, or_26_out, and_18_out);
  or or_40 (or_40_out, and_19_out, or_29_out);
  and and_21 (and_21_out, or_31_out, T3);
  and and_22 (and_22_out, or_32_out, T4);
  and and_23 (and_23_out, or_33_out, T3);
  and and_24 (and_24_out, or_34_out, T4);
  and and_25 (and_25_out, or_35_out, T3);
  and and_26 (and_26_out, or_36_out, T4);
  and and_27 (and_27_out, or_37_out, T3);
  and and_28 (and_28_out, or_38_out, T4);
  and and_29 (and_29_out, or_39_out, T3);
  and and_30 (and_30_out, or_40_out, T4);
  or or_41 (AX, and_21_out, and_22_out, and_4_out);
  or or_42 (BX, and_23_out, and_24_out, and_8_out);
  or or_43 (CX, and_25_out, and_26_out, and_12_out);
  or or_44 (DX, and_27_out, and_28_out, and_16_out);
  or or_45 (EX, and_29_out, and_30_out, and_20_out);
endmodule

module INSTRUCTION (
  input  T3,
  input  T4,
  input  T5,
  input  M0,
  input  M1,
  input  M2,
  input  M3,
  input  M4,
  input  M5,
  input  M6,
  input  M7,
  input  M8,
  input  M9,
  input  M10,
  input  M11,
  input  M12,
  input  M13,
  input  M14,
  input  M15,
  input  M16,
  input  M17,
  input  M18,
  input  M19,
  input  M20,
  input  M21,
  input  M22,
  input  M23,
  input  M24,
  input  M25,
  input  M26,
  input  M27,
  input  M28,
  input  M29,
  input  M30,
  input  M31,
  input  M32,
  input  M33,
  input  M34,
  input  M35,
  input  M36,
  input  M37,
  input  M38,
  input  M39,
  input  M40,
  input  M41,
  input  M42,
  input  M43,
  input  M44,
  input  M45,
  input  M46,
  input  M47,
  input  M48,
  input  M49,
  input  M50,
  input  M51,
  input  M52,
  input  M53,
  input  M54,
  input  M55,
  input  M56,
  input  M57,
  input  M58,
  input  M59,
  input  M60,
  input  M61,
  input  M62,
  input  M63,
  input  M64,
  input  M65,
  input  M66,
  input  M67,
  input  M68,
  input  M69,
  input  M70,
  input  M71,
  input  M72,
  input  M73,
  input  M74,
  input  M75,
  input  M76,
  input  M77,
  input  M78,
  input  M79,
  input  M80,
  input  M81,
  input  M82,
  input  M83,
  input  M84,
  input  M85,
  input  M86,
  input  M87,
  input  M88,
  input  M89,
  input  M90,
  input  M91,
  input  M92,
  input  M93,
  input  M94,
  input  M95,
  input  M96,
  input  M97,
  input  M98,
  input  M99,
  input  M100,
  input  M101,
  input  M102,
  input  M103,
  input  M104,
  input  M105,
  input  M106,
  input  M107,
  input  M108,
  input  M109,
  input  M110,
  input  M111,
  input  M112,
  input  M113,
  input  M114,
  input  M115,
  input  M116,
  input  M117,
  input  M118,
  input  M119,
  input  M120,
  input  M121,
  input  M122,
  input  M123,
  input  M124,
  input  M125,
  input  M126,
  input  M127,
  input  M128,
  input  M129,
  input  M130,
  input  M131,
  input  M132,
  input  M133,
  input  M134,
  input  M135,
  input  M136,
  input  M137,
  input  M138,
  input  M139,
  input  M140,
  input  M141,
  input  M142,
  input  M143,
  input  M144,
  input  M145,
  input  M146,
  input  M147,
  input  M148,
  input  M149,
  input  M150,
  input  M151,
  input  M152,
  input  M153,
  input  M154,
  input  M155,
  input  M156,
  input  M157,
  input  M158,
  input  M159,
  input  M160,
  input  M161,
  input  M162,
  input  M163,
  input  M164,
  input  M165,
  input  M166,
  input  M167,
  input  M168,
  input  M169,
  input  M170,
  input  M171,
  input  M172,
  input  M173,
  input  M174,
  input  M175,
  input  M176,
  input  M177,
  input  M178,
  input  M179,
  input  M190,
  input  M191,
  input  M192,
  input  M193,
  input  M194,
  input  M195,
  output AND,
  output OR,
  output XOR,
  output ADD,
  output ADC,
  output SUB,
  output SBB,
  output MUL,
  output DIV,
  output CMP,
  output LOAD
);

  wire and_1_out, and_2_out, and_3_out, and_4_out, and_5_out, and_6_out, and_7_out, and_8_out, and_9_out,
       and_10_out, and_11_out, and_12_out, and_13_out, and_14_out, and_15_out, and_16_out, and_17_out,
       and_18_out, and_19_out, and_20_out, and_21_out, and_22_out, and_23_out, and_24_out, and_25_out,
       and_26_out, and_27_out, and_28_out, and_29_out, and_30_out, and_31_out, and_32_out, and_33_out,
       or_1_out, or_2_out, or_3_out, or_4_out, or_5_out, or_6_out, or_7_out, or_8_out, or_9_out, or_10_out,
       or_11_out, or_12_out, or_13_out, or_14_out, or_15_out, or_16_out, or_17_out, or_18_out, or_19_out,
       or_20_out, or_21_out, or_22_out, or_23_out, or_24_out, or_25_out, or_26_out, or_27_out, or_28_out,
       or_29_out, or_30_out, or_31_out, or_32_out, or_33_out;

  or or_1 (or_1_out, M16, M14, M13, M12, M11, M10);
  or or_2 (or_2_out, M15, M9, M8, M7, M6, M5);
  or or_3 (or_3_out, M4, M3, M2, M1, M0);
  or or_4 (or_4_out, M33, M31, M30, M29, M28, M27);
  or or_5 (or_5_out, M32, M26, M25, M24, M23, M22);
  or or_6 (or_6_out, M21, M20, M19, M18, M17);
  or or_7 (or_7_out, M50, M48, M47, M46, M45, M44);
  or or_8 (or_8_out, M49, M43, M42, M41, M40, M39);
  or or_9 (or_9_out, M38, M37, M36, M35, M34);
  or or_10 (or_10_out, M67, M65, M64, M63, M62, M61);
  or or_11 (or_11_out, M66, M60, M59, M58, M57, M56);
  or or_12 (or_12_out, M55, M54, M53, M52, M51);
  or or_13 (or_13_out, M84, M82, M81, M80, M79, M78);
  or or_14 (or_14_out, M83, M77, M76, M75, M74, M73);
  or or_15 (or_15_out, M72, M71, M70, M69, M68);
  or or_16 (or_16_out, M101, M99, M98, M97, M96, M95);
  or or_17 (or_17_out, M100, M94, M93, M92, M91, M90);
  or or_18 (or_18_out, M89, M88, M87, M86, M85);
  or or_19 (or_19_out, M118, M116, M115, M114, M113, M112);
  or or_20 (or_20_out, M117, M111, M110, M109, M108, M107);
  or or_21 (or_21_out, M106, M105, M104, M103, M102);
  or or_22 (or_22_out, M135, M133, M132, M131, M130, M129);
  or or_23 (or_23_out, M134, M128, M127, M126, M125, M124);
  or or_24 (or_24_out, M123, M122, M121, M120, M119);
  or or_25 (or_25_out, M152, M150, M149, M148, M147, M146);
  or or_26 (or_26_out, M151, M145, M144, M143, M142, M141);
  or or_27 (or_27_out, M140, M139, M138, M137, M136);
  or or_28 (or_28_out, M169, M167, M166, M165, M164, M163);
  or or_29 (or_29_out, M168, M162, M161, M160, M159, M158);
  or or_30 (or_30_out, M157, M156, M155, M154, M153);
  or or_31 (or_31_out, M195, M194, M193, M192, M191, M190);
  or or_32 (or_32_out, M179, M178, M177, M176, M175);
  or or_33 (or_33_out, M174, M173, M172, M171, M170);
  and and_1 (and_1_out, or_1_out, T3);
  and and_2 (and_2_out, or_2_out, T4);
  and and_3 (and_3_out, or_3_out, T5);
  and and_4 (and_4_out, or_4_out, T3);
  and and_5 (and_5_out, or_5_out, T4);
  and and_6 (and_6_out, or_6_out, T5);
  and and_7 (and_7_out, or_7_out, T3);
  and and_8 (and_8_out, or_8_out, T4);
  and and_9 (and_9_out, or_9_out, T5);
  and and_10 (and_10_out, or_10_out, T3);
  and and_11 (and_11_out, or_11_out, T4);
  and and_12 (and_12_out, or_12_out, T5);
  and and_13 (and_13_out, or_13_out, T3);
  and and_14 (and_14_out, or_14_out, T4);
  and and_15 (and_15_out, or_15_out, T5);
  and and_16 (and_16_out, or_16_out, T3);
  and and_17 (and_17_out, or_17_out, T4);
  and and_18 (and_18_out, or_18_out, T5);
  and and_19 (and_19_out, or_19_out, T3);
  and and_20 (and_20_out, or_20_out, T4);
  and and_21 (and_21_out, or_21_out, T5);
  and and_22 (and_22_out, or_22_out, T3);
  and and_23 (and_23_out, or_23_out, T4);
  and and_24 (and_24_out, or_24_out, T5);
  and and_25 (and_25_out, or_25_out, T3);
  and and_26 (and_26_out, or_26_out, T4);
  and and_27 (and_27_out, or_27_out, T5);
  and and_28 (and_28_out, or_28_out, T3);
  and and_29 (and_29_out, or_29_out, T4);
  and and_30 (and_30_out, or_30_out, T5);
  and and_31 (and_31_out, or_31_out, T3);
  and and_32 (and_32_out, or_32_out, T4);
  and and_33 (and_33_out, or_33_out, T5);
  or or_34 (AND, and_1_out, and_2_out, and_3_out);
  or or_35 (OR, and_4_out, and_5_out, and_6_out);
  or or_36 (XOR, and_7_out, and_8_out, and_9_out);
  or or_37 (ADD, and_10_out, and_11_out, and_12_out);
  or or_38 (ADC, and_13_out, and_14_out, and_15_out);
  or or_39 (SUB, and_16_out, and_17_out, and_18_out);
  or or_40 (SBB, and_19_out, and_20_out, and_21_out);
  or or_41 (MUL, and_22_out, and_23_out, and_24_out);
  or or_42 (DIV, and_25_out, and_26_out, and_27_out);
  or or_43 (CMP, and_28_out, and_29_out, and_30_out);
  or or_44 (LOAD, and_31_out, and_32_out, and_33_out);
endmodule
