// Logisim project Microprocessor.circ as structural Verilog
module AND_1 (
  input  AX,
  input  BX,
  input  CX,
  input  DX,
  input  EX,
  input  DR,
  input  IR,
  input  AX__DR,
  input  BX__DR,
  input  CX__DR,
  input  DX__DR,
  input  EX__DR,
  input  AX__IR,
  input  BX__IR,
  input  CX__IR,
  input  DX__IR,
  input  EX__IR,
  input  AX__BX,
  input  AX__CX,
  input  AX__DX,
  input  AX__EX,
  input  BX__CX,
  input  BX__DX,
  input  BX__EX,
  input  CX__DX,
  input  CX__EX,
  input  DX__EX,
  output OUTPUT
);

  wire and_1_out, and_2_out, and_3_out, and_4_out, and_5_out, and_6_out, and_7_out, and_8_out, and_9_out,
       and_10_out, and_11_out, and_12_out, and_13_out, and_14_out, and_15_out, and_16_out, and_17_out,
       and_18_out, and_19_out, and_20_out;

  and and_1 (and_1_out, AX__DR, DR, AX);
  and and_2 (and_2_out, BX__DR, DR, BX);
  and and_3 (and_3_out, CX__DR, DR, CX);
  and and_4 (and_4_out, DX__DR, DR, DX);
  and and_5 (and_5_out, EX__DR, DR, EX);
  and and_6 (and_6_out, AX__IR, IR, AX);
  and and_7 (and_7_out, BX__IR, IR, BX);
  and and_8 (and_8_out, CX__IR, IR, CX);
  and and_9 (and_9_out, DX__IR, IR, DX);
  and and_10 (and_10_out, EX__IR, IR, EX);
  and and_11 (and_11_out, AX__BX, BX, AX);
  and and_12 (and_12_out, AX__CX, CX, AX);
  and and_13 (and_13_out, AX__DX, DX, AX);
  and and_14 (and_14_out, AX__EX, EX, AX);
  and and_15 (and_15_out, BX__CX, CX, BX);
  and and_16 (and_16_out, BX__DX, DX, BX);
  and and_17 (and_17_out, BX__EX, EX, BX);
  and and_18 (and_18_out, CX__DX, DX, CX);
  and and_19 (and_19_out, CX__EX, EX, CX);
  and and_20 (and_20_out, DX__EX, EX, CX);
  or or_1 (OUTPUT, and_1_out, and_2_out, and_3_out, and_4_out, and_5_out, and_6_out, and_7_out, and_8_out, and_9_out, and_10_out, and_11_out, and_12_out, and_13_out, and_14_out, and_15_out, and_16_out, and_17_out, and_18_out, and_19_out, and_20_out);
endmodule

module OR_1 (
  input  AX,
  input  BX,
  input  CX,
  input  DX,
  input  EX,
  input  DR,
  input  IR,
  input  AX__DR,
  input  BX__DR,
  input  CX__DR,
  input  DX__DR,
  input  EX__DR,
  input  AX__IR,
  input  BX__IR,
  input  CX__IR,
  input  DX__IR,
  input  EX__IR,
  input  AX__BX,
  input  AX__CX,
  input  AX__DX,
  input  AX__EX,
  input  BX__CX,
  input  BX__DX,
  input  BX__EX,
  input  CX__DX,
  input  CX__EX,
  input  DX__EX,
  output OUTPUT
);

  wire and_1_out, and_2_out, and_3_out, and_4_out, and_5_out, and_6_out, and_7_out, and_8_out, and_9_out,
       and_10_out, and_11_out, and_12_out, and_13_out, and_14_out, and_15_out, and_16_out, and_17_out,
       and_18_out, and_19_out, and_20_out, or_1_out, or_2_out, or_3_out, or_4_out, or_5_out, or_6_out,
       or_7_out, or_8_out, or_9_out, or_10_out, or_11_out, or_12_out, or_13_out, or_14_out, or_15_out,
       or_16_out, or_17_out, or_18_out, or_19_out, or_20_out;

  or or_1 (or_1_out, DR, AX);
  or or_2 (or_2_out, DR, BX);
  or or_3 (or_3_out, DR, CX);
  or or_4 (or_4_out, DR, DX);
  or or_5 (or_5_out, DR, EX);
  or or_6 (or_6_out, IR, AX);
  or or_7 (or_7_out, IR, BX);
  or or_8 (or_8_out, IR, CX);
  or or_9 (or_9_out, IR, DX);
  or or_10 (or_10_out, IR, EX);
  or or_11 (or_11_out, BX, AX);
  or or_12 (or_12_out, CX, AX);
  or or_13 (or_13_out, DX, AX);
  or or_14 (or_14_out, EX, AX);
  or or_15 (or_15_out, CX, BX);
  or or_16 (or_16_out, DX, BX);
  or or_17 (or_17_out, EX, BX);
  or or_18 (or_18_out, DX, CX);
  or or_19 (or_19_out, EX, CX);
  or or_20 (or_20_out, EX, CX);
  and and_1 (and_1_out, AX__DR, or_1_out);
  and and_2 (and_2_out, BX__DR, or_2_out);
  and and_3 (and_3_out, CX__DR, or_3_out);
  and and_4 (and_4_out, DX__DR, or_4_out);
  and and_5 (and_5_out, EX__DR, or_5_out);
  and and_6 (and_6_out, AX__IR, or_6_out);
  and and_7 (and_7_out, BX__IR, or_7_out);
  and and_8 (and_8_out, CX__IR, or_8_out);
  and and_9 (and_9_out, DX__IR, or_9_out);
  and and_10 (and_10_out, EX__IR, or_10_out);
  and and_11 (and_11_out, AX__BX, or_11_out);
  and and_12 (and_12_out, AX__CX, or_12_out);
  and and_13 (and_13_out, AX__DX, or_13_out);
  and and_14 (and_14_out, AX__EX, or_14_out);
  and and_15 (and_15_out, BX__CX, or_15_out);
  and and_16 (and_16_out, BX__DX, or_16_out);
  and and_17 (and_17_out, BX__EX, or_17_out);
  and and_18 (and_18_out, CX__DX, or_18_out);
  and and_19 (and_19_out, CX__EX, or_19_out);
  and and_20 (and_20_out, DX__EX, or_20_out);
  or or_21 (OUTPUT, and_1_out, and_2_out, and_3_out, and_4_out, and_5_out, and_6_out, and_7_out, and_8_out, and_9_out, and_10_out, and_11_out, and_12_out, and_13_out, and_14_out, and_15_out, and_16_out, and_17_out, and_18_out, and_19_out, and_20_out);
endmodule

module XOR_1 (
  input  AX,
  input  BX,
  input  CX,
  input  DX,
  input  EX,
  input  DR,
  input  IR,
  input  AX__DR,
  input  BX__DR,
  input  CX__DR,
  input  DX__DR,
  input  EX__DR,
  input  AX__IR,
  input  BX__IR,
  input  CX__IR,
  input  DX__IR,
  input  EX__IR,
  input  AX__BX,
  input  AX__CX,
  input  AX__DX,
  input  AX__EX,
  input  BX__CX,
  input  BX__DX,
  input  BX__EX,
  input  CX__DX,
  input  CX__EX,
  input  DX__EX,
  output OUTPUT
);

  wire and_1_out, and_2_out, and_3_out, and_4_out, and_5_out, and_6_out, and_7_out, and_8_out, and_9_out,
       and_10_out, and_11_out, and_12_out, and_13_out, and_14_out, and_15_out, and_16_out, and_17_out,
       and_18_out, and_19_out, and_20_out, xor_1_out, xor_2_out, xor_3_out, xor_4_out, xor_5_out, xor_6_out,
       xor_7_out, xor_8_out, xor_9_out, xor_10_out, xor_11_out, xor_12_out, xor_13_out, xor_14_out,
       xor_15_out, xor_16_out, xor_17_out, xor_18_out, xor_19_out, xor_20_out;

  xor xor_1 (xor_1_out, DR, AX);
  xor xor_2 (xor_2_out, DR, BX);
  xor xor_3 (xor_3_out, DR, CX);
  xor xor_4 (xor_4_out, DR, DX);
  xor xor_5 (xor_5_out, DR, EX);
  xor xor_6 (xor_6_out, IR, AX);
  xor xor_7 (xor_7_out, IR, BX);
  xor xor_8 (xor_8_out, IR, CX);
  xor xor_9 (xor_9_out, IR, DX);
  xor xor_10 (xor_10_out, IR, EX);
  xor xor_11 (xor_11_out, BX, AX);
  xor xor_12 (xor_12_out, CX, AX);
  xor xor_13 (xor_13_out, DX, AX);
  xor xor_14 (xor_14_out, EX, AX);
  xor xor_15 (xor_15_out, CX, BX);
  xor xor_16 (xor_16_out, DX, BX);
  xor xor_17 (xor_17_out, EX, BX);
  xor xor_18 (xor_18_out, DX, CX);
  xor xor_19 (xor_19_out, EX, CX);
  xor xor_20 (xor_20_out, EX, CX);
  and and_1 (and_1_out, AX__DR, xor_1_out);
  and and_2 (and_2_out, BX__DR, xor_2_out);
  and and_3 (and_3_out, CX__DR, xor_3_out);
  and and_4 (and_4_out, DX__DR, xor_4_out);
  and and_5 (and_5_out, EX__DR, xor_5_out);
  and and_6 (and_6_out, AX__IR, xor_6_out);
  and and_7 (and_7_out, BX__IR, xor_7_out);
  and and_8 (and_8_out, CX__IR, xor_8_out);
  and and_9 (and_9_out, DX__IR, xor_9_out);
  and and_10 (and_10_out, EX__IR, xor_10_out);
  and and_11 (and_11_out, AX__BX, xor_11_out);
  and and_12 (and_12_out, AX__CX, xor_12_out);
  and and_13 (and_13_out, AX__DX, xor_13_out);
  and and_14 (and_14_out, AX__EX, xor_14_out);
  and and_15 (and_15_out, BX__CX, xor_15_out);
  and and_16 (and_16_out, BX__DX, xor_16_out);
  and and_17 (and_17_out, BX__EX, xor_17_out);
  and and_18 (and_18_out, CX__DX, xor_18_out);
  and and_19 (and_19_out, CX__EX, xor_19_out);
  and and_20 (and_20_out, DX__EX, xor_20_out);
  or or_1 (OUTPUT, and_1_out, and_2_out, and_3_out, and_4_out, and_5_out, and_6_out, and_7_out, and_8_out, and_9_out, and_10_out, and_11_out, and_12_out, and_13_out, and_14_out, and_15_out, and_16_out, and_17_out, and_18_out, and_19_out, and_20_out);
endmodule

module LOGIC_INPUT_4to1 (
  input  [3:0] AX,
  input  [3:0] BX,
  input  [3:0] CX,
  input  [3:0] DX,
  input  [3:0] EX,
  input  [3:0] DR,
  input  [3:0] IR,
  output AX3,
  output BX3,
  output CX3,
  output DX3,
  output EX3,
  output DR3,
  output IR3,
  output AX2,
  output BX2,
  output CX2,
  output DX2,
  output EX2,
  output DR2,
  output IR2,
  output AX1,
  output BX1,
  output CX1,
  output DX1,
  output EX1,
  output DR1,
  output IR1,
  output AX0,
  output BX0,
  output CX0,
  output DX0,
  output EX0,
  output DR0,
  output IR0
);


  assign AX0 = AX[0];
  assign AX1 = AX[1];
  assign AX2 = AX[2];
  assign AX3 = AX[3];
  assign BX0 = BX[0];
  assign BX1 = BX[1];
  assign BX2 = BX[2];
  assign BX3 = BX[3];
  assign CX0 = CX[0];
  assign CX1 = CX[1];
  assign CX2 = CX[2];
  assign CX3 = CX[3];
  assign DR0 = DR[0];
  assign DR1 = DR[1];
  assign DR2 = DR[2];
  assign DR3 = DR[3];
  assign DX0 = DX[0];
  assign DX1 = DX[1];
  assign DX2 = DX[2];
  assign DX3 = DX[3];
  assign EX0 = EX[0];
  assign EX1 = EX[1];
  assign EX2 = EX[2];
  assign EX3 = EX[3];
  assign IR0 = IR[0];
  assign IR1 = IR[1];
  assign IR2 = IR[2];
  assign IR3 = IR[3];
endmodule
